// Logisim project Lab6Lib.circ as structural Verilog: 2 circuits, main circuit FF_D
module FF_D (
  input  D,
  input  CLK,
  input  Reset_Inv,
  output Q,
  output Q_Inv
);

  wire not_1_out;

  D_Flip_Flop d_ff_1 (.D(D), .clk(CLK), .Q(Q), .Qn(Q_Inv), .preset(1'b0), .reset(not_1_out));
  not not_1 (not_1_out, Reset_Inv);
endmodule

module DEC_2_4 (
  input  A0,
  input  A1,
  output D0,
  output D1,
  output D2,
  output D3
);

  Decoder #(.select(2), .enable("false")) decoder_1 (.out0(D0), .out1(D1), .out2(D2), .out3(D3), .sel({A1, A0}));
endmodule
