// Logisim project lab6.circ as structural Verilog: 1 circuit, main circuit main
module main (
  input  A,
  input  RESET,
  output Q1,
  output Q0
);

  wire clock_1_out, dec_2_4_1_d0, dec_2_4_1_d1, dec_2_4_1_d2, dec_2_4_1_d3, ff_d_2_q_inv, xor_1_out,
       xor_2_out;

  Clock clock_1 (.out(clock_1_out));
  xor xor_1 (xor_1_out, Q0, A);
  xor xor_2 (xor_2_out, Q1, xor_1_out);
  FF_D ff_d_1 (.Q(Q1), .CLK(clock_1_out), .D(xor_2_out), .Reset_Inv(RESET));  // open: Q_Inv
  FF_D ff_d_2 (.Q(Q0), .CLK(clock_1_out), .D(ff_d_2_q_inv), .Reset_Inv(RESET), .Q_Inv(ff_d_2_q_inv));
  DEC_2_4 dec_2_4_1 (.D2(dec_2_4_1_d2), .D1(dec_2_4_1_d1), .D0(dec_2_4_1_d0), .A1(Q1), .A0(Q0), .D3(dec_2_4_1_d3));
  LED led_1 (.in(dec_2_4_1_d0));
  LED led_2 (.in(dec_2_4_1_d0));
  LED led_3 (.in(dec_2_4_1_d1));
  LED led_4 (.in(dec_2_4_1_d2));
  LED led_5 (.in(dec_2_4_1_d2));
  LED led_6 (.in(dec_2_4_1_d3));
  LED led_7 (.in(dec_2_4_1_d3));

  // Notes on the sheet:
  //   CLK
endmodule
