// Logisim project Lab9.circ as structural Verilog: 2 circuits, main circuit Complete_System
module Complete_System (
  input  Manual_Auto,
  input  [2:0] Endereco,
  input  [7:0] Dados,
  input  Clear,
  input  Read_Write,
  input  Enable
);

  wire and_1_out, clock_1_out, or_1_out;
  wire [2:0] ctr_3bit_1_q2_q0, mux_1_y;
  wire [7:0] ram_8x8_1_dout;

  Clock clock_1 (.out(clock_1_out));
  // Probe on Endereco
  // Probe on Dados
  and and_1 (and_1_out, ~Manual_Auto, Read_Write);  // AND_Gate
  or or_1 (or_1_out, Manual_Auto, Enable);
  CTR_3Bit ctr_3bit_1 (.Reset(Manual_Auto), .CLK(clock_1_out), .Q2_Q0(ctr_3bit_1_q2_q0));
  MUX mux_1 (.Y(mux_1_y), .I1(ctr_3bit_1_q2_q0), .S(Manual_Auto), .I0(Endereco));
  RAM_8x8 ram_8x8_1 (.Dout(ram_8x8_1_dout), .Din(Dados), .Enable(or_1_out), .Read_Write(and_1_out));  // open: Addr
  // Probe on ram_8x8_1_dout
  TTY tty_1 (.data(ram_8x8_1_dout[6:0]), .clk(clock_1_out), .we(Manual_Auto), .clr(Clear));
endmodule

module RAM_8x8 (
  input  [2:0] Addr,
  input  [7:0] Din,
  input  Enable,
  input  Read_Write,
  output [7:0] Dout
);

  wire [3:0] ram_4x4_1_data_out, ram_4x4_2_data_out;

  RAM_4x4 ram_4x4_1 (
    .Data_In(Din[3:0]), .Addr(Addr[1:0]), .Enable(Enable), .Data_Out(ram_4x4_1_data_out),
    .Read_Write(Read_Write));
  RAM_4x4 ram_4x4_2 (
    .Data_In(Din[7:4]), .Addr(Addr[1:0]), .Enable(Enable), .Data_Out(ram_4x4_2_data_out),
    .Read_Write(Read_Write));
  RAM_2x8 ram_2x8_1 (
    .Read_Write(Read_Write), .Enable(Enable), .Data_out(Dout),
    .Data_in({ram_4x4_2_data_out, ram_4x4_1_data_out}), .Addr(Addr[2]));
endmodule
