// Logisim project LabControlUnit.circ as structural Verilog: 2 circuits, main circuit CTR_3Bit
module CTR_3Bit (
  input  CLK,
  input  Reset,
  output [2:0] Q2_Q0
);

  wire and_1_out, not_1_out, not_2_out, xor_1_out, xor_2_out;

  D_Flip_Flop d_ff_1 (.D(not_1_out), .clk(CLK), .Q(Q2_Q0[0]), .preset(1'b0), .reset(not_2_out));  // open: Qn
  not not_1 (not_1_out, Q2_Q0[0]);
  not not_2 (not_2_out, Reset);
  xor xor_1 (xor_1_out, Q2_Q0[1], Q2_Q0[0]);
  D_Flip_Flop d_ff_2 (.D(xor_1_out), .clk(CLK), .Q(Q2_Q0[1]), .preset(1'b0), .reset(not_2_out));  // open: Qn
  and and_1 (and_1_out, Q2_Q0[0], Q2_Q0[1]);
  D_Flip_Flop d_ff_3 (.D(xor_2_out), .clk(CLK), .Q(Q2_Q0[2]), .preset(1'b0), .reset(not_2_out));  // open: Qn
  xor xor_2 (xor_2_out, Q2_Q0[2], and_1_out);
endmodule

module MUX (
  input  [2:0] I0,
  input  [2:0] I1,
  input  S,
  output [2:0] Y
);

  Multiplexer #(.width(3), .enable("false")) multiplexer_1 (.in0(I0), .in1(I1), .out(Y), .sel(S));
endmodule
