// Logisim project LabRamModules.circ as structural Verilog: 3 circuits, main circuit Memory_Cell_1bit
module Memory_Cell_1bit (
  input  Din,
  input  R_W,
  input  En,
  output Dout
);

  wire and_1_out, d_ff_1_q;

  D_Flip_Flop #(.trigger("high")) d_ff_1 (
    .D(Din), .clk(and_1_out), .Q(d_ff_1_q), .preset(1'b0), .reset(1'b0));  // open: Qn
  and and_1 (and_1_out, R_W, En);
  assign Dout = En ? d_ff_1_q : 1'bz;  // Controlled_Buffer controlled_buffer_1
endmodule

module RAM_4x4 (
  input  [3:0] Data_In,
  input  Enable,
  input  [1:0] Addr,
  input  Read_Write,
  output [3:0] Data_Out
);

  wire decoder_1_out0, decoder_1_out1, decoder_1_out2, decoder_1_out3;

  Decoder #(.select(2)) decoder_1 (
    .out0(decoder_1_out0), .out1(decoder_1_out1), .out2(decoder_1_out2), .out3(decoder_1_out3), .sel(Addr),
    .en(Enable));
  Memory_Cell_1bit memory_cell_1bit_1 (.En(decoder_1_out0), .R_W(Read_Write), .Din(Data_In[3]), .Dout(Data_Out[3]));
  Memory_Cell_1bit memory_cell_1bit_2 (.En(decoder_1_out1), .R_W(Read_Write), .Din(Data_In[3]), .Dout(Data_Out[3]));
  Memory_Cell_1bit memory_cell_1bit_3 (.En(decoder_1_out2), .R_W(Read_Write), .Din(Data_In[3]), .Dout(Data_Out[3]));
  Memory_Cell_1bit memory_cell_1bit_4 (.En(decoder_1_out3), .R_W(Read_Write), .Din(Data_In[3]), .Dout(Data_Out[3]));
  Memory_Cell_1bit memory_cell_1bit_5 (.En(decoder_1_out0), .R_W(Read_Write), .Din(Data_In[2]), .Dout(Data_Out[2]));
  Memory_Cell_1bit memory_cell_1bit_6 (.En(decoder_1_out1), .R_W(Read_Write), .Din(Data_In[2]), .Dout(Data_Out[2]));
  Memory_Cell_1bit memory_cell_1bit_7 (.En(decoder_1_out2), .R_W(Read_Write), .Din(Data_In[2]), .Dout(Data_Out[2]));
  Memory_Cell_1bit memory_cell_1bit_8 (.En(decoder_1_out3), .R_W(Read_Write), .Din(Data_In[2]), .Dout(Data_Out[2]));
  Memory_Cell_1bit memory_cell_1bit_9 (.En(decoder_1_out0), .R_W(Read_Write), .Din(Data_In[1]), .Dout(Data_Out[1]));
  Memory_Cell_1bit memory_cell_1bit_10 (.En(decoder_1_out1), .R_W(Read_Write), .Din(Data_In[1]), .Dout(Data_Out[1]));
  Memory_Cell_1bit memory_cell_1bit_11 (.En(decoder_1_out2), .R_W(Read_Write), .Din(Data_In[1]), .Dout(Data_Out[1]));
  Memory_Cell_1bit memory_cell_1bit_12 (.En(decoder_1_out3), .R_W(Read_Write), .Din(Data_In[1]), .Dout(Data_Out[1]));
  Memory_Cell_1bit memory_cell_1bit_13 (.En(decoder_1_out0), .R_W(Read_Write), .Din(Data_In[0]), .Dout(Data_Out[0]));
  Memory_Cell_1bit memory_cell_1bit_14 (.En(decoder_1_out1), .R_W(Read_Write), .Din(Data_In[0]), .Dout(Data_Out[0]));
  Memory_Cell_1bit memory_cell_1bit_15 (.En(decoder_1_out2), .R_W(Read_Write), .Din(Data_In[0]), .Dout(Data_Out[0]));
  Memory_Cell_1bit memory_cell_1bit_16 (.En(decoder_1_out3), .R_W(Read_Write), .Din(Data_In[0]), .Dout(Data_Out[0]));
endmodule

module RAM_2x8 (
  input  [7:0] Data_in,
  input  Addr,
  input  Enable,
  input  Read_Write,
  output [7:0] Data_out
);

  wire and_1_out, and_2_out;

  and and_1 (and_1_out, ~Addr, Enable);  // AND_Gate
  and and_2 (and_2_out, Addr, Enable);
  Memory_Cell_1bit memory_cell_1bit_1 (.En(and_1_out), .R_W(Read_Write), .Din(Data_in[7]), .Dout(Data_out[7]));
  Memory_Cell_1bit memory_cell_1bit_2 (.En(and_2_out), .R_W(Read_Write), .Din(Data_in[7]), .Dout(Data_out[7]));
  Memory_Cell_1bit memory_cell_1bit_3 (.En(and_1_out), .R_W(Read_Write), .Din(Data_in[6]), .Dout(Data_out[6]));
  Memory_Cell_1bit memory_cell_1bit_4 (.En(and_2_out), .R_W(Read_Write), .Din(Data_in[6]), .Dout(Data_out[6]));
  Memory_Cell_1bit memory_cell_1bit_5 (.En(and_1_out), .R_W(Read_Write), .Din(Data_in[5]), .Dout(Data_out[5]));
  Memory_Cell_1bit memory_cell_1bit_6 (.En(and_2_out), .R_W(Read_Write), .Din(Data_in[5]), .Dout(Data_out[5]));
  Memory_Cell_1bit memory_cell_1bit_7 (.En(and_1_out), .R_W(Read_Write), .Din(Data_in[4]), .Dout(Data_out[4]));
  Memory_Cell_1bit memory_cell_1bit_8 (.En(and_2_out), .R_W(Read_Write), .Din(Data_in[4]), .Dout(Data_out[4]));
  Memory_Cell_1bit memory_cell_1bit_9 (.En(and_1_out), .R_W(Read_Write), .Din(Data_in[3]), .Dout(Data_out[3]));
  Memory_Cell_1bit memory_cell_1bit_10 (.En(and_2_out), .R_W(Read_Write), .Din(Data_in[3]), .Dout(Data_out[3]));
  Memory_Cell_1bit memory_cell_1bit_11 (.En(and_1_out), .R_W(Read_Write), .Din(Data_in[2]), .Dout(Data_out[2]));
  Memory_Cell_1bit memory_cell_1bit_12 (.En(and_2_out), .R_W(Read_Write), .Din(Data_in[2]), .Dout(Data_out[2]));
  Memory_Cell_1bit memory_cell_1bit_13 (.En(and_1_out), .R_W(Read_Write), .Din(Data_in[1]), .Dout(Data_out[1]));
  Memory_Cell_1bit memory_cell_1bit_14 (.En(and_2_out), .R_W(Read_Write), .Din(Data_in[1]), .Dout(Data_out[1]));
  Memory_Cell_1bit memory_cell_1bit_15 (.En(and_1_out), .R_W(Read_Write), .Din(Data_in[0]), .Dout(Data_out[0]));
  Memory_Cell_1bit memory_cell_1bit_16 (.En(and_2_out), .R_W(Read_Write), .Din(Data_in[0]), .Dout(Data_out[0]));
endmodule
